// Logisim project TRIAL09_FINAL_CIRCUIT.circ as structural Verilog: 1 circuit, main circuit main
module main (
  input  D,
  input  E,
  input  [2:0] in_3,
  output out_4
);

  wire and_1_out, and_2_out, and_3_out, and_4_out, not_1_out, not_2_out, or_1_out;

  not not_1 (not_1_out, D);
  not not_2 (not_2_out, E);
  and and_1 (and_1_out, not_1_out, not_2_out);
  and and_2 (and_2_out, not_1_out, E);
  and and_3 (and_3_out, D, not_2_out);
  and and_4 (and_4_out, not_1_out, not_2_out);
  or or_1 (or_1_out, and_1_out, and_2_out, and_3_out);
  Multiplexer #(.select(3)) multiplexer_1 (
    .in0(1'b1), .in1(or_1_out), .in2(or_1_out), .in3(and_4_out), .in4(or_1_out), .in5(and_4_out),
    .in6(and_4_out), .in7(1'b0), .out(out_4), .sel(in_3));
endmodule
